// Logisim project ASYNCH.circ as structural Verilog: 1 circuit, main circuit main
module main (
  input  in_1,
  input  in_2
);

  wire clock_1_out, clock_2_out, t_ff_1_q, t_ff_1_qn, t_ff_2_q, t_ff_2_qn, t_ff_3_qn, t_ff_4_q, t_ff_4_qn,
       t_ff_5_q, t_ff_5_qn, t_ff_6_q, t_ff_6_qn, t_ff_7_q;

  Clock clock_1 (.out(clock_1_out));
  Clock clock_2 (.out(clock_2_out));
  T_Flip_Flop t_ff_1 (.clk(clock_1_out), .T(in_1), .Q(t_ff_1_q), .Qn(t_ff_1_qn));  // open: preset, reset, en
  T_Flip_Flop t_ff_2 (.clk(t_ff_1_qn), .T(in_1), .Q(t_ff_2_q), .Qn(t_ff_2_qn));  // open: preset, reset, en
  T_Flip_Flop t_ff_3 (.clk(t_ff_2_qn), .T(in_1), .Qn(t_ff_3_qn));  // open: Q, preset, reset, en
  T_Flip_Flop t_ff_4 (.clk(clock_2_out), .T(in_2), .Q(t_ff_4_q), .Qn(t_ff_4_qn));  // open: preset, reset, en
  T_Flip_Flop t_ff_5 (.clk(t_ff_4_qn), .T(in_2), .Q(t_ff_5_q), .Qn(t_ff_5_qn));  // open: preset, reset, en
  T_Flip_Flop t_ff_6 (.clk(t_ff_5_qn), .T(in_2), .Q(t_ff_6_q), .Qn(t_ff_6_qn));  // open: preset, reset, en
  T_Flip_Flop t_ff_7 (.clk(t_ff_6_qn), .T(in_2), .Q(t_ff_7_q));  // open: Qn, preset, reset, en
  LED led_1 (.in(t_ff_1_q));
  LED led_2 (.in(t_ff_2_q));
  LED led_3 (.in(t_ff_3_qn));
  LED led_4 (.in(t_ff_4_q));
  LED led_5 (.in(t_ff_5_q));
  LED led_6 (.in(t_ff_6_q));
  LED led_7 (.in(t_ff_7_q));

  // Notes on the sheet:
  //   TWO BIT ASYNCHRONOUS COUNTER
  //   4 BIT ASYNCHRONOUS COUNTER
  //   Q0
  //   Q1
  //   Q3
  //   q0
  //   q1
  //   q2
  //   q3
endmodule
