// Logisim project FA.circ as structural Verilog: 1 circuit, main circuit main
module main (
  input  a,
  input  b,
  input  Cin
);

  wire and_1_out, and_2_out, and_3_out, not_1_out, or_1_out, xor_1_out;

  not not_1 (not_1_out, a);
  and and_1 (and_1_out, not_1_out, Cin);
  and and_2 (and_2_out, not_1_out, b);
  and and_3 (and_3_out, b, Cin);
  ExactlyOne xor_1 (.out(xor_1_out), .in0(a), .in2(b), .in4(Cin));
  LED led_1 (.in(xor_1_out));
  or or_1 (or_1_out, and_1_out, and_2_out, and_3_out);
  LED led_2 (.in(or_1_out));

  // Notes on the sheet:
  //   SIMULATION OF FULL ADDER
  //   DIFFERENCE
  //   Cout
endmodule
