// Logisim project FLIP FLOP AND LATCH.circ as structural Verilog: 1 circuit, main circuit main
module main (
  input  in_1,
  input  R,
  input  in_3,
  input  S,
  input  in_5,
  input  in_6,
  input  in_7,
  input  R_2,
  input  E,
  input  in_10,
  input  in_11,
  input  S_2,
  input  J_K_FLIP_FLOP,
  input  in_14,
  input  in_15,
  input  in_16,
  input  in_17,
  input  in_18,
  input  in_19
);

  wire clock_1_out, clock_2_out, clock_3_out, clock_4_out, clock_5_out, clock_6_out, clock_7_out, d_ff_1_q,
       j_k_ff_1_q, j_k_ff_1_qn, j_k_ff_3_q, j_k_ff_3_qn, nand_1_out, nand_2_out, nand_3_out, nand_4_out,
       nand_5_out, nand_6_out, nand_7_out, nand_8_out, nand_9_out, nand_10_out, nand_11_out, nand_12_out,
       nand_13_out, nand_14_out, nand_15_out, nand_16_out, nand_17_out, nand_18_out, nand_19_out,
       nand_20_out, nor_1_out, nor_2_out, not_1_out, not_2_out, not_3_out, s_r_ff_1_q, s_r_ff_1_qn, t_ff_1_q;

  Clock clock_1 (.out(clock_1_out));
  nand nand_1 (nand_1_out, R_2, E);
  nand nand_2 (nand_2_out, E, S_2);
  J_K_Flip_Flop j_k_ff_1 (
    .J(in_16), .clk(clock_1_out), .K(in_17), .Q(j_k_ff_1_q), .Qn(j_k_ff_1_qn));  // open: preset, en, reset
  nor nor_1 (nor_1_out, R, nor_2_out);
  nor nor_2 (nor_2_out, nor_1_out, S);
  not not_1 (not_1_out, clock_1_out);
  J_K_Flip_Flop j_k_ff_2 (
    .J(j_k_ff_1_q), .clk(not_1_out), .K(j_k_ff_1_qn), .Q(in_17), .Qn(in_16));  // open: preset, en, reset
  LED led_1 (.in(nor_1_out));
  LED led_2 (.in(nor_2_out));
  nand nand_3 (nand_3_out, nand_1_out, nand_4_out);
  nand nand_4 (nand_4_out, nand_3_out, nand_2_out);
  LED led_3 (.in(in_17));
  LED led_4 (.in(in_16));
  LED led_5 (.in(nand_3_out));
  LED led_6 (.in(nand_4_out));
  not not_2 (not_2_out, in_1);
  Clock clock_2 (.out(clock_2_out));
  nand nand_5 (nand_5_out, in_1, in_3);
  nand nand_6 (nand_6_out, in_3, not_2_out);
  Clock clock_3 (.out(clock_3_out));
  Clock clock_4 (.out(clock_4_out));
  Clock clock_5 (.out(clock_5_out));
  T_Flip_Flop t_ff_1 (.clk(clock_3_out), .T(in_6), .Q(t_ff_1_q));  // open: Qn, preset, reset, en
  nand nand_7 (nand_7_out, nand_20_out, in_18, clock_2_out);
  nand nand_8 (nand_8_out, in_19, nand_19_out);
  nand nand_9 (nand_9_out, nand_5_out, nand_10_out);
  nand nand_10 (nand_10_out, nand_9_out, nand_6_out);
  LED led_7 (.in(t_ff_1_q));
  LED led_8 (.in(d_ff_1_q));
  D_Flip_Flop d_ff_1 (.clk(clock_4_out), .D(in_10), .Q(d_ff_1_q));  // open: Qn, preset, en, reset
  J_K_Flip_Flop j_k_ff_3 (
    .J(J_K_FLIP_FLOP), .clk(clock_5_out), .K(in_14), .Q(j_k_ff_3_q), .Qn(j_k_ff_3_qn));  // open: preset, en, reset
  LED led_9 (.in(j_k_ff_3_q));
  LED led_10 (.in(j_k_ff_3_qn));
  LED led_11 (.in(nand_9_out));
  LED led_12 (.in(nand_10_out));
  Clock clock_6 (.out(clock_6_out));
  nand nand_11 (nand_11_out, nand_7_out, nand_12_out);
  nand nand_12 (nand_12_out, nand_11_out, nand_8_out);
  not not_3 (not_3_out, clock_2_out);
  Clock clock_7 (.out(clock_7_out));
  nand nand_13 (nand_13_out, nand_18_out, in_11, clock_6_out);
  nand nand_14 (nand_14_out, clock_6_out, in_15, nand_17_out);
  S_R_Flip_Flop s_r_ff_1 (
    .S(in_5), .clk(clock_7_out), .R(in_7), .Q(s_r_ff_1_q), .Qn(s_r_ff_1_qn));  // open: preset, reset, en
  nand nand_15 (nand_15_out, nand_11_out, not_3_out);
  nand nand_16 (nand_16_out, not_3_out, nand_12_out);
  LED led_13 (.in(s_r_ff_1_q));
  LED led_14 (.in(s_r_ff_1_qn));
  nand nand_17 (nand_17_out, nand_13_out, nand_18_out);
  nand nand_18 (nand_18_out, nand_17_out, nand_14_out);
  LED led_15 (.in(nand_17_out));
  LED led_16 (.in(nand_18_out));
  nand nand_19 (nand_19_out, nand_15_out, nand_20_out);
  nand nand_20 (nand_20_out, nand_19_out, nand_16_out);
  LED led_17 (.in(nand_19_out));
  LED led_18 (.in(nand_20_out));

  // Notes on the sheet:
  //   SR LATCH 
  //   GATED SR LATCH
  //   JK MASTER SLAVE
  //   GATED D LATCH
  //   T FLIP FLOP
  //   D FLIP FLOP
  //   JK MASTER SLAVE
endmodule
