// Logisim project FS NOR.circ as structural Verilog: 1 circuit, main circuit main
module main (
  input  in_1,
  input  in_2,
  input  in_3
);

  wire nor_1_out, nor_2_out, nor_3_out, nor_4_out, nor_5_out, nor_6_out, nor_7_out, nor_8_out, nor_9_out,
       nor_10_out, nor_11_out, nor_12_out;

  nor nor_1 (nor_1_out, in_1, in_2);
  nor nor_2 (nor_2_out, in_1, nor_1_out);
  nor nor_3 (nor_3_out, nor_1_out, in_2);
  nor nor_4 (nor_4_out, nor_2_out, nor_3_out);
  nor nor_5 (nor_5_out, nor_4_out, nor_4_out);
  nor nor_6 (nor_6_out, nor_5_out, in_3);
  nor nor_7 (nor_7_out, nor_5_out, nor_6_out);
  nor nor_8 (nor_8_out, nor_6_out, in_3);
  nor nor_9 (nor_9_out, nor_7_out, nor_8_out);
  nor nor_10 (nor_10_out, nor_2_out, nor_7_out);
  LED led_1 (.in(nor_11_out));
  nor nor_11 (nor_11_out, nor_10_out, nor_10_out);
  nor nor_12 (nor_12_out, nor_9_out, nor_9_out);
  LED led_2 (.in(nor_12_out));

  // Notes on the sheet:
  //   FULL SUBTRACTOR USING NOR
  //   BORROW
  //   DIFFERENCE
endmodule
