// Logisim project HA.circ as structural Verilog: 1 circuit, main circuit main
module main (
  input  a,
  input  b
);

  wire and_1_out, xor_1_out;

  xor xor_1 (xor_1_out, a, b);
  and and_1 (and_1_out, a, b);
  LED led_1 (.in(xor_1_out));
  LED led_2 (.in(and_1_out));

  // Notes on the sheet:
  //   SIMULATION OF HALF ADDER
  //   SUM
  //   22-10-2020
  //   CARRY
endmodule
