// Logisim project MOD 6 8 USING JK.circ as structural Verilog: 1 circuit, main circuit main
module main (
  input  in_1,
  input  in_2
);

  wire and_1_out, and_2_out, and_3_out, clock_1_out, clock_2_out, j_k_ff_1_q, j_k_ff_1_qn, j_k_ff_2_q,
       j_k_ff_3_q, j_k_ff_4_q, j_k_ff_5_q, j_k_ff_6_q;

  and and_1 (and_1_out, j_k_ff_4_q, j_k_ff_5_q);
  Clock clock_1 (.out(clock_1_out));
  and and_2 (and_2_out, j_k_ff_3_q, j_k_ff_6_q);
  Clock clock_2 (.out(clock_2_out));
  J_K_Flip_Flop j_k_ff_1 (
    .J(and_1_out), .clk(clock_1_out), .K(j_k_ff_5_q), .Q(j_k_ff_1_q), .Qn(j_k_ff_1_qn));  // open: preset, en, reset
  J_K_Flip_Flop j_k_ff_2 (
    .J(and_2_out), .clk(clock_2_out), .K(and_2_out), .Q(j_k_ff_2_q));  // open: Qn, preset, en, reset
  LED led_1 (.in(j_k_ff_1_q));
  LED led_2 (.in(j_k_ff_2_q));
  and and_3 (and_3_out, j_k_ff_1_qn, j_k_ff_5_q);
  J_K_Flip_Flop j_k_ff_3 (
    .J(j_k_ff_6_q), .clk(clock_2_out), .K(j_k_ff_6_q), .Q(j_k_ff_3_q));  // open: Qn, preset, en, reset
  J_K_Flip_Flop j_k_ff_4 (
    .J(and_3_out), .clk(clock_1_out), .K(j_k_ff_5_q), .Q(j_k_ff_4_q));  // open: Qn, preset, en, reset
  LED led_3 (.in(j_k_ff_3_q));
  LED led_4 (.in(j_k_ff_4_q));
  LED led_5 (.in(j_k_ff_5_q));
  J_K_Flip_Flop j_k_ff_5 (.J(in_1), .clk(clock_1_out), .K(in_1), .Q(j_k_ff_5_q));  // open: Qn, preset, en, reset
  LED led_6 (.in(j_k_ff_6_q));
  J_K_Flip_Flop j_k_ff_6 (.J(in_2), .clk(clock_2_out), .K(in_2), .Q(j_k_ff_6_q));  // open: Qn, preset, en, reset

  // Notes on the sheet:
  //   MOD 6 SYNCHRONOUS COUNTER USING JK
  //   MOD 8 SYNCHRONOUS COUNTER USING JK
endmodule
