// Logisim project MOD 6 USING T.circ as structural Verilog: 1 circuit, main circuit main
module main (
  input  in_1
);

  wire and_1_out, and_2_out, and_3_out, clock_1_out, or_1_out, t_ff_1_q, t_ff_1_qn, t_ff_2_q, t_ff_3_q,
       t_ff_3_qn;

  and and_1 (and_1_out, t_ff_1_q, t_ff_3_qn);
  and and_2 (and_2_out, t_ff_2_q, t_ff_3_q);
  Clock clock_1 (.out(clock_1_out));
  or or_1 (or_1_out, and_1_out, and_2_out);
  T_Flip_Flop t_ff_1 (.clk(clock_1_out), .T(or_1_out), .Q(t_ff_1_q), .Qn(t_ff_1_qn));  // open: preset, reset, en
  LED led_1 (.in(t_ff_1_q));
  and and_3 (and_3_out, t_ff_1_qn, t_ff_3_q);
  LED led_2 (.in(t_ff_2_q));
  T_Flip_Flop t_ff_2 (.clk(clock_1_out), .T(and_3_out), .Q(t_ff_2_q));  // open: Qn, preset, reset, en
  T_Flip_Flop t_ff_3 (.clk(clock_1_out), .T(in_1), .Q(t_ff_3_q), .Qn(t_ff_3_qn));  // open: preset, reset, en
  LED led_3 (.in(t_ff_3_q));

  // Notes on the sheet:
  //   MOD 6 USING T FLIP FLOP
  //   Qa
  //   Qb
  //   Qc
endmodule
