// Logisim project MOD 8 COUNTER USING D.circ as structural Verilog: 1 circuit, main circuit main
module main (
);

  wire and_1_out, and_2_out, clock_1_out, d_ff_1_q, d_ff_2_q, d_ff_3_q, d_ff_3_qn, or_1_out, xor_1_out,
       xor_2_out;

  xor xor_1 (xor_1_out, d_ff_2_q, d_ff_1_q);
  Clock clock_1 (.out(clock_1_out));
  and and_1 (and_1_out, xor_1_out, d_ff_3_q);
  and and_2 (and_2_out, d_ff_1_q, d_ff_3_qn);
  or or_1 (or_1_out, and_1_out, and_2_out);
  D_Flip_Flop d_ff_1 (.clk(clock_1_out), .D(or_1_out), .Q(d_ff_1_q));  // open: Qn, preset, en, reset
  LED led_1 (.in(d_ff_1_q));
  xor xor_2 (xor_2_out, d_ff_2_q, d_ff_3_q);
  D_Flip_Flop d_ff_2 (.clk(clock_1_out), .D(xor_2_out), .Q(d_ff_2_q));  // open: Qn, preset, en, reset
  LED led_2 (.in(d_ff_2_q));
  D_Flip_Flop d_ff_3 (.clk(clock_1_out), .D(d_ff_3_qn), .Q(d_ff_3_q), .Qn(d_ff_3_qn));  // open: preset, en, reset
  LED led_3 (.in(d_ff_3_q));

  // Notes on the sheet:
  //   MOD 8 COUNTER USING D FLIP FLOP
  //   qa
  //   qb
  //   qc
endmodule
