// Logisim project PLEXERS.circ as structural Verilog: 1 circuit, main circuit main
module main (
  input  in_1,
  input  in_2,
  input  in_3,
  input  in_4,
  input  in_5,
  input  [1:0] in_6,
  input  in_7,
  input  [1:0] in_8,
  input  in_9,
  input  in_10,
  input  in_11,
  input  in_12,
  input  in_13,
  input  in_14,
  input  in_15,
  input  in_16,
  input  [2:0] in_17,
  input  [2:0] in_18,
  input  [1:0] in_19,
  input  [2:0] in_20,
  input  in_21,
  input  in_22,
  input  in_23,
  input  in_24,
  input  in_25,
  input  in_26,
  input  in_27,
  input  in_28,
  input  in_29,
  input  in_30,
  input  in_31,
  input  in_32
);

  wire decoder_1_out0, decoder_1_out1, decoder_1_out2, decoder_1_out3, decoder_2_out0, decoder_2_out1,
       decoder_2_out2, decoder_2_out3, decoder_2_out4, decoder_2_out5, decoder_2_out6, decoder_2_out7,
       demultiplexer_1_out0, demultiplexer_1_out1, demultiplexer_1_out2, demultiplexer_1_out3,
       demultiplexer_2_out0, demultiplexer_2_out1, demultiplexer_2_out2, demultiplexer_2_out3,
       demultiplexer_2_out4, demultiplexer_2_out5, demultiplexer_2_out6, demultiplexer_2_out7,
       multiplexer_1_out, multiplexer_2_out;
  wire [1:0] priority_encoder_1_out;
  wire [2:0] priority_encoder_2_out;

  Decoder #(.select(2)) decoder_1 (
    .out0(decoder_1_out0), .out1(decoder_1_out1), .out2(decoder_1_out2), .out3(decoder_1_out3), .sel(in_19));  // open: en
  Priority_Encoder #(.select(2)) priority_encoder_1 (
    .in0(in_21), .in1(in_22), .in2(in_23), .in3(in_25), .out(priority_encoder_1_out));  // open: gs, en_out, en_in
  LED led_1 (.in(decoder_1_out0));
  LED led_2 (.in(decoder_1_out1));
  LED led_3 (.in(decoder_1_out2));
  LED led_4 (.in(decoder_1_out3));
  Multiplexer #(.select(2)) multiplexer_1 (
    .in0(in_1), .in1(in_2), .in2(in_4), .in3(in_5), .out(multiplexer_1_out), .sel(in_8));  // open: en
  LED led_5 (.in(multiplexer_1_out));
  Multiplexer #(.select(3)) multiplexer_2 (
    .in0(in_7), .in1(in_9), .in2(in_10), .in3(in_11), .in4(in_13), .in5(in_14), .in6(in_15), .in7(in_16),
    .out(multiplexer_2_out), .sel(in_18));  // open: en
  LED led_6 (.in(multiplexer_2_out));
  LED led_7 (.in(priority_encoder_1_out[0]));
  LED led_8 (.in(priority_encoder_1_out[1]));
  Demultiplexer #(.select(2)) demultiplexer_1 (
    .out0(demultiplexer_1_out0), .out1(demultiplexer_1_out1), .out2(demultiplexer_1_out2),
    .out3(demultiplexer_1_out3), .in(in_3), .sel(in_6));  // open: en
  Demultiplexer #(.select(3)) demultiplexer_2 (
    .out0(demultiplexer_2_out0), .out1(demultiplexer_2_out1), .out2(demultiplexer_2_out2),
    .out3(demultiplexer_2_out3), .out4(demultiplexer_2_out4), .out5(demultiplexer_2_out5),
    .out6(demultiplexer_2_out6), .out7(demultiplexer_2_out7), .in(in_12), .sel(in_17));  // open: en
  Decoder #(.select(3)) decoder_2 (
    .out0(decoder_2_out0), .out1(decoder_2_out1), .out2(decoder_2_out2), .out3(decoder_2_out3),
    .out4(decoder_2_out4), .out5(decoder_2_out5), .out6(decoder_2_out6), .out7(decoder_2_out7), .sel(in_20));  // open: en
  LED led_9 (.in(demultiplexer_1_out0));
  LED led_10 (.in(demultiplexer_1_out1));
  LED led_11 (.in(demultiplexer_1_out2));
  LED led_12 (.in(demultiplexer_1_out3));
  Priority_Encoder priority_encoder_2 (
    .in0(in_24), .in1(in_26), .in2(in_27), .in3(in_28), .in4(in_29), .in5(in_30), .in6(in_31), .in7(in_32),
    .out(priority_encoder_2_out));  // open: en_in, gs, en_out
  LED led_13 (.in(demultiplexer_2_out0));
  LED led_14 (.in(demultiplexer_2_out1));
  LED led_15 (.in(demultiplexer_2_out2));
  LED led_16 (.in(demultiplexer_2_out3));
  LED led_17 (.in(demultiplexer_2_out4));
  LED led_18 (.in(demultiplexer_2_out5));
  LED led_19 (.in(demultiplexer_2_out6));
  LED led_20 (.in(demultiplexer_2_out7));
  LED led_21 (.in(decoder_2_out0));
  LED led_22 (.in(decoder_2_out1));
  LED led_23 (.in(decoder_2_out2));
  LED led_24 (.in(decoder_2_out3));
  LED led_25 (.in(decoder_2_out4));
  LED led_26 (.in(decoder_2_out5));
  LED led_27 (.in(decoder_2_out6));
  LED led_28 (.in(decoder_2_out7));
  LED led_29 (.in(priority_encoder_2_out[0]));
  LED led_30 (.in(priority_encoder_2_out[1]));
  LED led_31 (.in(priority_encoder_2_out[2]));

  // Notes on the sheet:
  //    2:4 DECODER
  //   4:2 PRIORITY ENCODER
  //   4:1 MUX
  //   8:1 MUX
  //   1:8 MUX
  //   3:8 DECODER
  //   1:4 MUX
  //   8:3 PRIORITY ENCODER
  //   LSB
  //   MSB
endmodule
