// Logisim project REALISATION.circ as structural Verilog: 1 circuit, main circuit main
module main (
  input  S1,
  input  S0,
  input  a,
  input  b,
  input  D0,
  input  c,
  input  D1,
  input  a_2,
  input  D2,
  input  b_2,
  input  D3,
  input  c_2,
  input  S1_2,
  input  S0_2,
  input  E,
  input  I,
  input  in_17,
  input  in_18,
  input  in_19,
  input  in_20,
  input  in_21,
  input  in_22
);

  wire and_1_out, and_2_out, and_3_out, and_6_out, and_11_out, and_12_out, and_13_out, and_14_out,
       and_15_out, and_16_out, and_17_out, and_18_out, not_1_out, not_2_out, not_3_out, not_4_out, not_5_out,
       not_6_out, not_7_out, not_8_out, not_9_out, not_10_out, not_11_out, not_12_out, not_13_out, or_1_out,
       or_2_out, xor_1_out, xor_2_out;

  not not_1 (not_1_out, b_2);
  not not_2 (not_2_out, c_2);
  not not_3 (not_3_out, in_19);
  not not_4 (not_4_out, in_20);
  not not_5 (not_5_out, in_21);
  not not_6 (not_6_out, not_3_out);
  not not_7 (not_7_out, not_4_out);
  not not_8 (not_8_out, not_5_out);
  not not_9 (not_9_out, in_22);
  xor xor_1 (xor_1_out, a, b);
  and and_1 (and_1_out, a_2, not_2_out);
  and and_2 (and_2_out, not_1_out, a_2);
  and and_3 (and_3_out, not_1_out, not_2_out);
  LED led_1 (.in(xor_2_out));
  xor xor_2 (xor_2_out, xor_1_out, c);
  // AND_Gate and_4 has open pins: in0=not_9_out, in1=not_5_out, in2=not_4_out, in3=not_3_out, in4=in_17, out=open
  or or_1 (or_1_out, and_1_out, and_2_out, and_3_out);
  // AND_Gate and_5 has open pins: in0=not_9_out, in1=not_8_out, in2=not_4_out, in3=not_3_out, in4=in_18, out=open
  LED led_2 (.in(or_1_out));
  // AND_Gate and_6 has open pins: out=and_6_out
  not not_10 (not_10_out, S1_2);
  // AND_Gate and_7 has open pins: in2=and_6_out, out=open
  // AND_Gate and_8 is placed but not wired
  not not_11 (not_11_out, S1);
  not not_12 (not_12_out, S0_2);
  // AND_Gate and_9 is placed but not wired
  not not_13 (not_13_out, S0);
  // AND_Gate and_10 is placed but not wired
  and and_11 (and_11_out, D0, not_11_out, not_13_out);
  and and_12 (and_12_out, D1, not_11_out, S0);
  and and_13 (and_13_out, D2, S1, not_13_out);
  and and_14 (and_14_out, D3, S1, S0);
  LED led_3 (.in(and_15_out));
  and and_15 (and_15_out, I, E, not_12_out, not_10_out);
  LED led_4 (.in(and_16_out));
  and and_16 (and_16_out, I, E, S0_2, not_10_out);
  LED led_5 (.in(and_17_out));
  and and_17 (and_17_out, I, E, S1_2, not_12_out);
  LED led_6 (.in(and_18_out));
  and and_18 (and_18_out, I, E, S1_2, S0_2);
  // AND_Gate and_19 is placed but not wired
  LED led_7 (.in(or_2_out));
  or or_2 (or_2_out, and_11_out, and_12_out, and_13_out, and_14_out);

  // Notes on the sheet:
  //   MSB
  //   LSB
  //   MSB
  //   LSB
  //   REALIZATION OF BOOLEAN EXPRESSION
  //   OUTPUT
  //   OUTPUT
  //   MSB
  //   MSB
  //   LSB
  //   4:1 MUX
  //   LSB
  //   1:4 DEMUX
endmodule
